// Digital circuit UTSNO13.dig as structural Verilog
module UTSNO13 (
  input  X,
  input  Y,
  input  Z
);

  wire and_1_out, and_2_out, and_3_out, not_1_out, not_2_out, not_3_out, or_1_out;

  not not_1 (not_1_out, Y);
  not not_2 (not_2_out, Z);
  not not_3 (not_3_out, X);
  and and_1 (and_1_out, not_3_out, Y, Z);
  and and_2 (and_2_out, X, not_1_out);
  and and_3 (and_3_out, Y, not_2_out);
  or or_1 (or_1_out, and_1_out, and_2_out, and_3_out);
  LED A (.in(or_1_out));

  // Notes on the sheet:
  //   DHEITRA
  //   13. X'YZ+XY'+YZ'
endmodule
